# Fritzing sketch MSP430-Dojo-BoosterPack (saved by Fritzing 0.9.1b)
breadboards: 1

parts:
  U1 = 7-SEGMENT-DISPLAY [package=7-segment-display]
  8x = Resistor [tolerance=±5% resistance=150 package=THT]
  R2 = Resistor [tolerance=±5% resistance=150 package=THT]
  R3 = Resistor [tolerance=±5% resistance=150 package=THT]
  R4 = Resistor [tolerance=±5% resistance=150 package=THT]
  R5 = Resistor [tolerance=±5% resistance=150 package=THT]
  R6 = Resistor [tolerance=±5% resistance=150 package=THT]
  R7 = Resistor [tolerance=±5% resistance=150 package=THT]
  R8 = Resistor [tolerance=±5% resistance=150 package=THT]

nets:
  N1: U1.E, R4.Pin_1
  N2: U1.D, R5.Pin_1
  GND: U1.G1, U1.G2
  N3: U1.C, R3.Pin_1
  N4: U1.DP, R8.Pin_1
  N5: U1.B, R2.Pin_1
  N6: U1.A, 8x.Pin_1
  N7: U1.F, R7.Pin_1
  N8: U1.G, R6.Pin_1
  P1.0: 8x.Pin_0
  P1.1: R2.Pin_0
  P1.2: R3.Pin_0
  P1.4: R4.Pin_0
  P1.3: R5.Pin_0
  P1.6: R6.Pin_0
  P1.5: R7.Pin_0
  P1.7: R8.Pin_0
